// Logisim project Abacus_2_New.circ as structural Verilog
module northbridge (
  input  [7:0] B,
  input  [15:0] A
);

  wire BANKMAN, mmu_1_ram, mmu_1_rom, SOUTHBRIDGE;

  mmu mmu_1 (.B(B), .A(A), .BANK(BANKMAN), .ROM(mmu_1_rom), .RAM(mmu_1_ram), .IO(SOUTHBRIDGE));
endmodule

module mmu (
  input  [7:0] B,
  input  [15:0] A,
  output BANK,
  output ROM,
  output RAM,
  output IO
);

  wire and_1_out, and_2_out, and_3_out, and_5_out, and_6_out, and_7_out, nor_1_out, nor_2_out, not_1_out,
       not_2_out;

  not not_1 (not_1_out, B[6]);
  and and_1 (and_1_out, A[14], A[15]);
  not not_2 (not_2_out, A[13]);
  and and_2 (and_2_out, B[6], B[7]);
  and and_3 (and_3_out, not_1_out, B[7]);
  and and_4 (BANK, and_1_out, not_2_out);
  and and_5 (and_5_out, and_1_out, A[13]);
  and and_6 (and_6_out, B[5], and_3_out);
  or or_1 (ROM, and_5_out, and_7_out);
  and and_7 (and_7_out, BANK, and_6_out);
  or or_2 (RAM, nor_2_out, nor_1_out);
  nor nor_1 (nor_1_out, BANK, and_5_out);
  and and_8 (IO, BANK, and_2_out);
  nor nor_2 (nor_2_out, and_7_out, IO);
endmodule

module mmu_nano (
  input  [15:0] A,
  output ROM,
  output IO,
  output RAM
);

  wire and_1_out, nor_1_out;

  nor nor_1 (nor_1_out, A[13], A[13]);
  and and_1 (and_1_out, A[14], A[15]);
  and and_2 (IO, nor_1_out, and_1_out);
  and and_3 (ROM, and_1_out, A[13]);
  nor nor_2 (RAM, IO, ROM);
endmodule

module waitstategen (
  input  RAM,
  input  [3:0] RAM_WS,
  input  ROM,
  input  [3:0] ROM_WS,
  input  RST,
  input  LOAD,
  input  CLK,
  output HOLD_WS
);

  wire WS_COUNTER_carry;
  wire [3:0] controlled_buffer_1_out;

  assign controlled_buffer_1_out = RAM ? RAM_WS : 4'bz;  // Controlled_Buffer controlled_buffer_1
  assign controlled_buffer_1_out = ROM ? ROM_WS : 4'bz;  // Controlled_Buffer controlled_buffer_2
  Counter #(.max('hf), .width(4)) WS_COUNTER (
    .clr(RST), .load(LOAD), .up(1'b0), .count(1'b1), .clk(CLK), .D(controlled_buffer_1_out),
    .carry(WS_COUNTER_carry));  // open: Q
  not not_1 (HOLD_WS, WS_COUNTER_carry);
endmodule
